// Logisim project water_tank.circ as structural Verilog: 1 circuit, main circuit main
module main (
  input  S3,
  input  S2,
  input  S1,
  input  S0,
  input  RESET,
  input  CLOCK,
  output L1,
  output L0,
  output FULL,
  output PUMP,
  output R1,
  output R0,
  output CNT1,
  output CNT0,
  output ALARM,
  output SEG_A,
  output SEG_B,
  output SEG_C,
  output SEG_D,
  output SEG_E,
  output SEG_F,
  output SEG_G
);

  wire and_1_out, and_3_out, and_4_out, not_1_out, NQ0, NR1, or_2_out, or_3_out;

  LED S0_WATER (.in(S0));
  not not_1 (not_1_out, S2);
  and and_1 (and_1_out, not_1_out, S1);
  or or_1 (L0, and_1_out, S3);
  and and_2 (FULL, S2, L0);
  nand nand_1 (PUMP, S2, L0);
  LED PUMP_ON (.in(PUMP));
  D_Flip_Flop d_ff_1 (.clk(CLOCK), .D(S2), .Q(R1), .reset(RESET));  // open: Qn, preset, en
  D_Flip_Flop d_ff_2 (.clk(CLOCK), .D(L0), .Q(R0), .reset(RESET));  // open: Qn, preset, en
  or or_2 (or_2_out, CNT1, CNT0);
  or or_3 (or_3_out, NQ0, CNT1);
  not not_2 (NR1, R1);
  not not_3 (SEG_E, R0);
  and and_3 (and_3_out, or_2_out, FULL);
  and and_4 (and_4_out, or_3_out, FULL);
  or or_4 (SEG_A, R1, SEG_E);
  or or_5 (SEG_C, NR1, R0);
  nor nor_1 (SEG_F, R1, R0);
  D_Flip_Flop d_ff_3 (.clk(CLOCK), .D(and_3_out), .Q(CNT1), .reset(RESET));  // open: Qn, preset, en
  D_Flip_Flop d_ff_4 (.clk(CLOCK), .D(and_4_out), .Q(CNT0), .Qn(NQ0), .reset(RESET));  // open: preset, en
  and and_5 (ALARM, CNT1, CNT0);
  LED ALARM_LED (.in(ALARM));
  _7_Segment_Display u_7_segment_display_1 (
    .g(R1), .f(SEG_F), .a(SEG_A), .b(1'b1), .e(SEG_E), .d(SEG_A), .c(SEG_C), .dp(1'b0));

  assign L1 = S2;
  assign SEG_B = 1'b1;
  assign SEG_D = SEG_A;
  assign SEG_G = R1;

  // Other names for the same wires on the sheet: CLK = CLOCK; Q0 = CNT0; Q1 = CNT1; RST = RESET; SA = SEG_A;
  //   SC = SEG_C; NR0 = SEG_E; SE = SEG_E; SF = SEG_F; SG = R1

  // Notes on the sheet:
  //   IFT 211 MID-SEMESTER LAB - SMART WATER TANK MONITORING AND CONTROL SYSTEM
  //   Individual submission - pure digital logic, Logisim 2.7.1 format
  //   S0 empty-level probe: redundant in minimized logic (see K-maps); shown on LED
  //   STEP 1 - SENSOR ENCODING: L1 = S2 ; L0 = S1 AND NOT S2 OR S3
  //   STEP 2 - COMPARATOR: FULL = L1 AND L0 (level == 11)
  //   STEP 3 - PUMP CONTROL: PUMP = NAND(L1, L0) = NOT FULL
  //   STEP 4 - LEVEL REGISTER: two D flip-flops, clocked, async RESET
  //   STEP 5 - OVERFLOW COUNTER: counts while FULL=1, saturates at 3; ALARM = Q1 AND Q0
  //   STEP 6 - BCD TO 7-SEGMENT DECODER (from registered level R1 R0)
endmodule
